# Fritzing sketch rpi3_schematics_tf (saved by Fritzing 0.9.3b)
circuit board: 8.46667cm x 5.64444cm
breadboards: 1

parts:
  S1 = Pushbutton [package="[THT]"]
  R1 = Resistor [tolerance=±5% resistance=10k package="0402 [SMD]"]
  R2 = Resistor [tolerance=±5% resistance=470 package="0402 [SMD]"]
  LED1 = smd LED [color="Red (633nm)" package="1206 [SMD]"]
  Raspberry_Pi_1 = Raspberry Pi 3 [part_number=RPI-3-V1.2]
  U2 = TCM8240MD [package=tcm8240md]  # not connected
  J1 = Piezo Speaker  # not connected

nets:
  N1: S1.Pin_1, S1.Pin_2, LED1.cathode, Raspberry_Pi_1.GND
  N2: S1.Pin_3, S1.Pin_4, R1.Pin_1, Raspberry_Pi_1.GPIO21
  N3: R1.Pin_0, Raspberry_Pi_1.5V
  N4: R2.Pin_0, Raspberry_Pi_1.GPIO6
  N5: R2.Pin_1, LED1.anode
